// Logisim project main.circ as structural Verilog: 2 circuits, main circuit main
module main (
);

  // Buffer buffer_1 is placed but not wired
endmodule

module RAM_module (
  input  [7:0] DataIn,
  input  [7:0] Address,
  input  Reset,
  input  MemWrite,
  output [7:0] DataOut
);

  wire clock_1_out, not_1_out;

  Clock clock_1 (.out(clock_1_out));
  not not_1 (not_1_out, MemWrite);
  assign DataOut = MemWrite ? DataIn : 8'bz;  // Controlled_Buffer controlled_buffer_1
  RAM ram_1 (.addr(Address), .data(DataOut), .sel(1'b1), .clk(clock_1_out), .ld(not_1_out), .clr(Reset));
endmodule
